// Logisim project Hack_chaodao_Logisim.circ as structural Verilog
module Computer (
);

  wire clock, undriven, undriven_3;
  wire [14:0] undriven_4, undriven_5;
  wire [15:0] ram_1_dout, rom_1_data, undriven_2;

  RAM #(.addrWidth(15), .dataWidth(16)) ram_1 (
    .addr(undriven_4), .oe(undriven_3), .clk(undriven), .din(undriven_2), .dout(ram_1_dout));  // open: we
  Clock clock_1 (.out(clock));
  ROM #(.addrWidth(15), .dataWidth(16)) rom_1 (.addr(undriven_5), .data(rom_1_data));
  CPU cpu_1 (
    .outM_16(undriven_2), .writeM(undriven_3), .Instruction(rom_1_data), .inM(ram_1_dout),
    .PC_15(undriven_5), .address_15(undriven_4), .clock(clock));  // open: reset
endmodule

module CPU (
  input  [14:0] address_15,
  input  writeM,
  input  [15:0] Instruction,
  input  [15:0] inM,
  input  [15:0] outM_16,
  input  reset,
  input  clock,
  input  [14:0] PC_15
);

  wire and_2_out, and_3_out, and_4_out, and_5_out, and_6_out, and_7_out, not_1_out, not_2_out, not_3_out,
       not_4_out, or_1_out, or_2_out, or_3_out, undriven_2, undriven_3;
  wire [15:0] multiplexer_1_out, multiplexer_2_out, register_2_q;
  wire [15:15] register_1_q, undriven;

  and and_1 (writeM, Instruction[15], Instruction[3]);
  not not_1 (not_1_out, and_3_out);
  ProgramCounter programcounter_1 (
    .out_16({undriven[15], PC_15}), .inc(not_1_out), .load(and_3_out), .clock(clock), .reset(reset),
    .in_16({register_1_q[15], address_15}));
  not not_2 (not_2_out, Instruction[15]);
  Multiplexer #(.width(16)) multiplexer_1 (
    .in0(Instruction), .in1(outM_16), .out(multiplexer_1_out), .sel(Instruction[15]));
  and and_2 (and_2_out, Instruction[4], Instruction[15]);
  Register #(.width(16)) register_1 (
    .D(multiplexer_1_out), .en(or_1_out), .clk(clock), .Q({register_1_q[15], address_15}));  // open: clr
  or or_1 (or_1_out, Instruction[5], not_2_out);
  Register #(.width(16)) register_2 (.D(outM_16), .en(and_2_out), .clk(clock), .Q(register_2_q));  // open: clr
  and and_3 (and_3_out, Instruction[15], or_2_out);
  or or_2 (or_2_out, or_3_out, and_5_out);
  or or_3 (or_3_out, and_4_out, and_7_out);
  Multiplexer #(.width(16)) multiplexer_2 (
    .in0({register_1_q[15], address_15}), .in1(inM), .out(multiplexer_2_out), .sel(Instruction[12]));
  and and_4 (and_4_out, Instruction[2], undriven_2);
  and and_5 (and_5_out, Instruction[1], undriven_3);
  not not_3 (not_3_out, undriven_2);
  and and_6 (and_6_out, not_3_out, not_4_out);
  and and_7 (and_7_out, Instruction[0], and_6_out);
  ALU alu_1 (
    .zx(Instruction[11]), .zr(undriven_3), .ng(undriven_2), .X_16(register_2_q), .Y_16(multiplexer_2_out),
    .zy(Instruction[9]), .nx(Instruction[10]), .ny(Instruction[8]), .f(Instruction[7]), .no(Instruction[6]),
    .out(outM_16));
  not not_4 (not_4_out, undriven_3);
endmodule

module ALU (
  input  [15:0] X_16,
  input  [15:0] out,
  input  nx,
  input  f,
  input  no,
  input  zr,
  input  ng,
  input  [15:0] Y_16,
  input  zy,
  input  ny,
  output zx
);

  wire [15:0] adder_1_out, and_1_out, multiplexer_1_out, multiplexer_2_out, multiplexer_3_out,
       multiplexer_4_out, multiplexer_5_out, not_1_out, not_2_out, not_3_out;

  Multiplexer #(.width(16)) multiplexer_1 (.in0(X_16), .in1({16{1'b0}}), .out(multiplexer_1_out), .sel(zx));
  Multiplexer #(.width(16)) multiplexer_2 (.in0(Y_16), .in1({16{1'b0}}), .out(multiplexer_2_out), .sel(zy));
  assign not_1_out = ~multiplexer_1_out;  // NOT_Gate not_1, 16 bits wide
  assign not_2_out = ~multiplexer_2_out;  // NOT_Gate not_2, 16 bits wide
  Multiplexer #(.width(16)) multiplexer_3 (.in0(multiplexer_1_out), .in1(not_1_out), .out(multiplexer_3_out), .sel(nx));
  Multiplexer #(.width(16)) multiplexer_4 (.in0(multiplexer_2_out), .in1(not_2_out), .out(multiplexer_4_out), .sel(ny));
  Adder #(.width(16)) adder_1 (
    .a(multiplexer_3_out), .b(multiplexer_4_out), .out(adder_1_out), .cin(1'b0));  // open: cout
  assign and_1_out = multiplexer_3_out & multiplexer_4_out;  // AND_Gate and_1, 16 bits wide
  Multiplexer #(.width(16)) multiplexer_5 (.in0(adder_1_out), .in1(and_1_out), .out(multiplexer_5_out), .sel(f));
  assign not_3_out = ~multiplexer_5_out;  // NOT_Gate not_3, 16 bits wide
  Multiplexer #(.width(16)) multiplexer_6 (.in0(multiplexer_5_out), .in1(not_3_out), .out(out), .sel(no));
  Comparator #(.width(16)) comparator_1 (.a(out), .b({16{1'b0}}), .eq(zr), .lt(ng));  // open: gt
endmodule

module ProgramCounter (
  input  [15:0] out_16,
  input  inc,
  input  load,
  input  clock,
  input  reset,
  input  [15:0] in_16
);

  wire [15:0] adder_1_out, multiplexer_1_out, multiplexer_2_out, multiplexer_3_out;

  Adder #(.width(16)) adder_1 (.a(out_16), .b(16'h1), .out(adder_1_out));  // open: cin, cout
  Multiplexer #(.width(16)) multiplexer_1 (.in0(out_16), .in1(adder_1_out), .out(multiplexer_1_out), .sel(inc));
  Multiplexer #(.width(16)) multiplexer_2 (.in0(multiplexer_1_out), .in1(in_16), .out(multiplexer_2_out), .sel(load));
  Multiplexer #(.width(16)) multiplexer_3 (.in0(multiplexer_2_out), .in1(16'h1), .out(multiplexer_3_out), .sel(reset));
  Register #(.width(16)) register_1 (.D(multiplexer_3_out), .en(1'b1), .clk(clock), .Q(out_16));  // open: clr
endmodule
